# Fritzing sketch Time_Bomb_With_Selector (saved by Fritzing 0.9.3b)
breadboards: 1

parts:
  Part1 = Arduino Uno (Rev3)
  LCD1 = LCD screen
  J1 = Piezo Speaker
  R1 = Resistor [tolerance=±5% resistance=100 package=THT]
  R3 = Resistor [tolerance=±5% resistance=220 package=THT]
  R4 = Resistor [tolerance=±5% resistance=1k package=THT]
  R5 = Trimmer Potentiometer [maximum_resistance=10kΩ package=THT]
  S1 = Pushbutton [package="[THT]"]
  R6 = Resistor [tolerance=±5% resistance=10k package=THT]

nets:
  N1: Part1.A0, R5.wiper
  N2: Part1.D9_PWM, J1.pin2
  N3: Part1.D11_PWM/MOSI, LCD1.E
  N4: Part1.D12/MISO, LCD1.RS
  N5: Part1.D2, S1.Pin_3, S1.Pin_4, R6.Pin_0
  N6: Part1.D4, LCD1.DB4
  N7: Part1.D5_PWM, LCD1.DB5
  N8: Part1.D6_PWM, LCD1.DB6
  N9: Part1.D7, LCD1.DB7
  5V: Part1.5V, LCD1.VDD, R3.Pin_0
  GND: Part1.GND, LCD1.VSS, LCD1.R/W, LCD1.LED-, R1.Pin_1, R4.Pin_0
  N10: LCD1.V0, R4.Pin_1
  N11: LCD1.LED+, R3.Pin_1
  N12: J1.pin1, R1.Pin_0
  N13: R5.leg1, S1.Pin_1, S1.Pin_2, R6.Pin_1

notes:
  Parts required:
  19 x cables
  1x 100Ω resistor
  1x 220Ω resistor
  1x 1kΩ resistor
  1x 10kΩ potentiometer
  1x piezo buzzer
  1x UNO
  by Panos Koutsoumanis

// code stored in the sketch: a_presetup.ino
#include <LiquidCrystal.h>;
#include <CountUpDownTimer.h>;
int buzzFreq = 100;
int BuzzerPin = 9;
const int rs = 12, en = 11, d4 = 5, d5 = 4, d6 = 3, d7 = 2;
LiquidCrystal lcd(rs, en, d4, d5, d6, d7);
CountUpDownTimer T(DOWN);

// code stored in the sketch: a_variables.ino


// code stored in the sketch: b_setup.ino
void setup() { 
    pinMode(BuzzerPin,OUTPUT);
    Serial.begin(115200);
    T.SetTimer(0,10,0); //H,M,S
    T.StartTimer();
    lcd.begin(16,2);  //col,row

    
}

// code stored in the sketch: c_loop.ino
void loop() {
  T.Timer();

  if (T.TimeHasChanged() ){
    
    Serial.print(T.ShowMinutes());
    Serial.print(":");
    Serial.println(T.ShowSeconds());
    tone(BuzzerPin, 3000);
    delay(100);
    noTone(BuzzerPin);
    delay(900);
    lcd.setCursor(0, 0); //col, row
    lcd.print("you have");
    lcd.print(T.ShowMinutes());
    lcd.print(":");
    lcd.print(T.ShowSeconds());
    lcd.print(" to");
    lcd.setCursor(0, 1);
    lcd.print("clear the area");
  }
    
}

// code stored in the sketch: Time_Bomb.ino
/*
 * Project by Panos Koutsoumanis
 * last edited on 16/11/2019
 * 
 * Parts required:
 *   17x cables
 *   1x 100Ω resistor
 *   1x 220Ω resistor
 *   1x 10kΩ potentiometer
 *   1x piezo buzzer
 *   1x Arduino UNO (or any arduino with pwm)
 * 
 * Wiring:
 *   it is strongly advised to draw the 5V and ground lines from the UNO to the breadboard, since the pins on board are not enough for every device.
 *   lcd pin VSS to 5V
 *   lcd pin VDD to ground
 *   lcd pin RS to digital pin 12
 *   lcd pin Enable (E) to digital pin 11
 *   lcd pin Dataline 4 (D4) to digital pin 5
 *   lcd pin Dataline 5 (D5) to digital pin 4
 *   lcd pin Dataline 6 (D6) to digital pin 3
 *   lcd pin Dataline 7 (D7) to digital pin 2
 *   lcd pin contrast Vin (A) through 220Ω res to 5V
 *   lcd pin contrast Gnd (K) to ground
 *   10K potentiometer:
 *     Sides to 5V and Gnd
 *     Wiper (middle pin) to lcd pin contrast (V0)
 *   Buzzer:
 *     Vin pin (+) to digital pin 9
 *     Gnd pin (-) through 100Ω resistor to ground
 * 
 * Code: a_presetup tab contains variables and library setups
 *       b_setup tab contains the void setup(); code
 *       c_lopp tab contains the void loop(); code
 *       
 *       
 *     
*/
